// Logisim project finished_mips_cpu.circ as structural Verilog: 5 circuits, main circuit main
module main (
  input  Reset,
  input  Clear,
  input  clk
);

  wire and_1_out, funt_to_alu_1_jr, main_control_1_beq, main_control_1_bitextend, main_control_1_bne,
       main_control_1_j, main_control_1_jal, main_control_1_load, main_control_1_memtoreg,
       main_control_1_regwrite, main_control_1_store, next_pc_1_out_9, or_1_out;
  wire [3:0] funt_to_alu_1_aluop, multiplexer_3_out, opcode_to_alu_1_aluop;
  wire [4:0] mipsprogramrom_1_p2_2, mipsprogramrom_1_p2_3, multiplexer_5_out, multiplexer_7_out;
  wire [5:0] mipsprogramrom_1_p2_4;
  wire [20:0] mipsprogramrom_1_p2;
  wire [29:0] incrementer_1_p3;
  wire [31:0] bit_extender_1_out, bit_extender_2_out, mips_alu_1_p2, mips_alu_1_p5, mips_ram_1_p7,
       multiplexer_1_out, multiplexer_2_out, multiplexer_4_out, multiplexer_6_out, multiplexer_8_out,
       register_1_q, registerfile_1_p7, registerfile_1_p8;
  wire [31:2] next_pc_1_out_8;

  and and_1 (and_1_out, funt_to_alu_1_jr, ~or_1_out);  // AND_Gate
  Multiplexer #(.width(32), .enable("false")) multiplexer_1 (
    .in0({incrementer_1_p3, 2'b00}), .in1({next_pc_1_out_8, 2'b00}), .out(multiplexer_1_out),
    .sel(next_pc_1_out_9));
  funt_to_alu funt_to_alu_1 (.in_1(mipsprogramrom_1_p2[5:0]), .aluop(funt_to_alu_1_aluop), .jr(funt_to_alu_1_jr));
  Register #(.width(32), .trigger("falling")) register_1 (
    .D(multiplexer_2_out), .en(1'b1), .clk(clk), .Q(register_1_q), .clr(Reset));
  Multiplexer #(.width(32), .enable("false")) multiplexer_2 (
    .in0(multiplexer_1_out), .in1(registerfile_1_p7), .out(multiplexer_2_out), .sel(and_1_out));
  opcode_to_alu opcode_to_alu_1 (.in_1(mipsprogramrom_1_p2_4), .aluop(opcode_to_alu_1_aluop));
  Multiplexer #(.width(4), .enable("false")) multiplexer_3 (
    .in0(funt_to_alu_1_aluop), .in1(opcode_to_alu_1_aluop), .out(multiplexer_3_out), .sel(or_1_out));
  // Incrementer #(.width(30)) incrementer_1: pin names not known; wires that end beside it: 1'b1, register_1_q[31:2], incrementer_1_p3
  next_pc next_pc_1 (
    .in_6(registerfile_1_p7), .beq(main_control_1_beq), .out_9(next_pc_1_out_9), .bne(main_control_1_bne),
    .in_7(registerfile_1_p8), .j(main_control_1_j), .in_1(incrementer_1_p3), .out_8(next_pc_1_out_8),
    .in_4({mipsprogramrom_1_p2_3, mipsprogramrom_1_p2[20:11], mipsprogramrom_1_p2_2, mipsprogramrom_1_p2[5:0]}));
  main_control main_control_1 (
    .in_1(mipsprogramrom_1_p2_4), .RegWrite(main_control_1_regwrite), .Store(main_control_1_store),
    .Load(main_control_1_load), .MemToReg(main_control_1_memtoreg), .BitExtend(main_control_1_bitextend),
    .beq(main_control_1_beq), .bne(main_control_1_bne), .j(main_control_1_j), .jal(main_control_1_jal));
  // MIPSProgramROM mipsprogramrom_1: pin names not known; wires that end beside it: register_1_q, {mipsprogramrom_1_p2_4, mipsprogramrom_1_p2_3, mipsprogramrom_1_p2[20:11], mipsprogramrom_1_p2_2, mipsprogramrom_1_p2[5:0]}
  assign bit_extender_1_out = {{16{1'b0}}, {mipsprogramrom_1_p2[15:11], mipsprogramrom_1_p2_2, mipsprogramrom_1_p2[5:0]}};  // Bit_Extender bit_extender_1
  assign bit_extender_2_out = {{16{mipsprogramrom_1_p2[15]}}, {mipsprogramrom_1_p2[15:11], mipsprogramrom_1_p2_2, mipsprogramrom_1_p2[5:0]}};  // Bit_Extender bit_extender_2
  or or_1 (or_1_out, mipsprogramrom_1_p2_4[0], mipsprogramrom_1_p2_4[1], mipsprogramrom_1_p2_4[2], mipsprogramrom_1_p2_4[3], mipsprogramrom_1_p2_4[4], mipsprogramrom_1_p2_4[5]);
  Multiplexer #(.width(32), .enable("false")) multiplexer_4 (
    .in0(multiplexer_8_out), .in1({incrementer_1_p3, 2'b00}), .out(multiplexer_4_out),
    .sel(main_control_1_jal));
  Multiplexer #(.width(5), .enable("false")) multiplexer_5 (
    .in0(mipsprogramrom_1_p2[15:11]), .in1(mipsprogramrom_1_p2[20:16]), .out(multiplexer_5_out),
    .sel(or_1_out));
  Multiplexer #(.width(32), .enable("false")) multiplexer_6 (
    .in0(bit_extender_1_out), .in1(bit_extender_2_out), .out(multiplexer_6_out),
    .sel(main_control_1_bitextend));
  Multiplexer #(.width(5), .enable("false")) multiplexer_7 (
    .in0(multiplexer_5_out), .in1({5{1'b1}}), .out(multiplexer_7_out), .sel(main_control_1_jal));
  // RegisterFile #(.trigger("falling")) registerfile_1: pin names not known; wires that end beside it: multiplexer_4_out, clk, main_control_1_regwrite, multiplexer_7_out, mipsprogramrom_1_p2_3, mipsprogramrom_1_p2[20:16], registerfile_1_p7, registerfile_1_p8
  Multiplexer #(.width(32), .enable("false")) multiplexer_8 (
    .in0(mips_alu_1_p5), .in1(mips_ram_1_p7), .out(multiplexer_8_out), .sel(main_control_1_memtoreg));
  // Mips_ALU mips_alu_1: pin names not known; wires that end beside it: registerfile_1_p7, mips_alu_1_p2, multiplexer_3_out, mipsprogramrom_1_p2_2, mips_alu_1_p5
  Multiplexer #(.width(32), .enable("false")) multiplexer_9 (
    .in0(registerfile_1_p8), .in1(multiplexer_6_out), .out(mips_alu_1_p2), .sel(or_1_out));
  // MIPS_RAM #(.addrWidth(24)) mips_ram_1: pin names not known; wires that end beside it: mips_alu_1_p5[23:0], registerfile_1_p8, main_control_1_store, clk, main_control_1_load, Clear, mips_ram_1_p7

  // Notes on the sheet:
  //   ROM
  //   PC
  //   opcode
  //   RS
  //   RT
  //   RD
  //   shamt
  //   funct
  //   imm16
  //   imm26
  //   contents of mipsprogramrom_1 (hex, n*v repeats v):
  //   funkcija: subu $2, $4, $5 jr $31  main: addiu $8, $0, 4 ori $9, $0, 0xabcd sll $9, $9, 16 ori $9,
  //   $9, 0x1234 sw $9, 0($8) sw $9, 4($8) ori $10, $0, 4 addu $12, $8, $10 lw $13, 0($12) addu $5, $0,
  //   $13 bne   $5, $0, razlicito addiu $4, $5, -8 j     krajif razlicito: addiu $4, $5, 8 krajif:  jal
  //   funkcija sw $2, 8($8)  # Nakon izvrsenja programa u RAM memoriji bi trebalo da budu podaci: # adresa
  //   0: 0xabcd1234 # adresa 4: 0xabcd1234 # adresa 8: 0x00000008 # Ako je na adresi 8 vrijednost
  //   0xfffffff8 onda branch ne radi kako bi trebalo
  //   BitExtend
  //   RegWrite
  //   Register File
  //   jal
  //   ALU
  //   AluOP
  //   Store
  //   RAM
  //   Load
  //   MemToReg
endmodule

module main_control (
  input  [5:0] in_1,
  output RegWrite,
  output Store,
  output Load,
  output MemToReg,
  output BitExtend,
  output beq,
  output bne,
  output j,
  output jal
);

  wire and_2_out, and_3_out, and_4_out, and_5_out, and_8_out, not_1_out, not_2_out, not_3_out, not_4_out,
       not_5_out, not_6_out, not_7_out, not_8_out, not_9_out, not_10_out, not_11_out, not_12_out, not_13_out,
       not_14_out, not_15_out, not_16_out, not_17_out;

  not not_1 (not_1_out, in_1[3]);
  not not_2 (not_2_out, in_1[2]);
  not not_3 (not_3_out, in_1[1]);
  not not_4 (not_4_out, in_1[3]);
  not not_5 (not_5_out, in_1[2]);
  not not_6 (not_6_out, in_1[2]);
  not not_7 (not_7_out, in_1[1]);
  and and_1 (Store, in_1[5], in_1[3]);
  not not_8 (not_8_out, in_1[3]);
  not not_9 (not_9_out, in_1[3]);
  not not_10 (not_10_out, in_1[2]);
  not not_11 (not_11_out, in_1[3]);
  not not_12 (not_12_out, in_1[0]);
  not not_13 (not_13_out, in_1[3]);
  not not_14 (not_14_out, in_1[1]);
  not not_15 (not_15_out, in_1[5]);
  not not_16 (not_16_out, in_1[3]);
  not not_17 (not_17_out, in_1[5]);
  and and_2 (and_2_out, not_1_out, not_2_out, not_3_out);
  and and_3 (and_3_out, not_4_out, not_5_out, in_1[0]);
  and and_4 (and_4_out, not_6_out, not_7_out, in_1[0]);
  and and_5 (and_5_out, in_1[3], in_1[2]);
  and and_6 (Load, in_1[5], not_8_out);
  and and_7 (MemToReg, in_1[5], not_9_out);
  and and_8 (and_8_out, in_1[3], not_10_out);
  and and_9 (beq, not_11_out, in_1[2], not_12_out);
  and and_10 (bne, not_13_out, not_14_out, in_1[0]);
  and and_11 (j, not_15_out, not_16_out, in_1[1]);
  and and_12 (jal, not_17_out, in_1[1], in_1[0]);
  or or_1 (RegWrite, and_2_out, and_3_out, and_4_out, and_5_out);
  or or_2 (BitExtend, and_8_out, in_1[5]);
endmodule

module opcode_to_alu (
  input  [5:0] in_1,
  output [3:0] aluop
);

  wire not_1_out;

  not not_1 (not_1_out, in_1[0]);
  and and_1 (aluop[2], in_1[1], not_1_out);

  assign {aluop[3], aluop[1:0]} = {in_1[2], in_1[0], 1'b0};

  // Notes on the sheet:
  //   opcode
endmodule

module funt_to_alu (
  input  [5:0] in_1,
  output [3:0] aluop,
  output jr
);

  wire and_2_out, not_1_out, not_2_out;

  not not_1 (not_1_out, in_1[0]);
  and and_1 (aluop[1], in_1[5], in_1[0]);
  not not_2 (not_2_out, in_1[5]);
  or or_1 (aluop[3], in_1[2], and_2_out);
  and and_2 (and_2_out, in_1[5], not_1_out);
  and and_3 (aluop[0], not_2_out, in_1[0]);

  assign aluop[2] = in_1[1];
  assign jr = in_1[3];

  // Notes on the sheet:
  //   funct
endmodule

module next_pc (
  input  [29:0] in_1,
  input  beq,
  input  bne,
  input  [25:0] in_4,
  input  j,
  input  [31:0] in_6,
  input  [31:0] in_7,
  output [29:0] out_8,
  output out_9
);

  wire and_1_out, and_2_out, comparator_1_eq;
  wire [29:0] adder_1_out, bit_extender_1_out;

  assign bit_extender_1_out = {{14{in_4[15]}}, in_4[15:0]};  // Bit_Extender bit_extender_1
  Adder #(.width(30)) adder_1 (.a(in_1), .b(bit_extender_1_out), .out(adder_1_out));  // open: cin, cout
  Comparator #(.width(32)) comparator_1 (.a(in_6), .b(in_7), .eq(comparator_1_eq));  // open: gt, lt
  Multiplexer #(.width(30), .enable("false")) multiplexer_1 (
    .in0(adder_1_out), .in1({in_1[29:26], in_4}), .out(out_8), .sel(j));
  or or_1 (out_9, and_2_out, j, and_1_out);
  and and_1 (and_1_out, comparator_1_eq, beq);
  and and_2 (and_2_out, ~comparator_1_eq, bne);  // AND_Gate

  // Notes on the sheet:
  //   Inc PC
  //   Imm26
  //   BusA
  //   BusB
  //   NextAddress
endmodule
