// Logisim project lv1.circ as structural Verilog
module rs_latch (
  input  R,
  input  in_2,
  output out_3,
  output out_4
);

  nor nor_1 (out_3, R, out_4);
  nor nor_2 (out_4, out_3, in_2);
endmodule

module d_latch2 (
  input  in_1,
  input  in_2,
  output out_3,
  output out_4
);

  wire and_1_out, and_2_out, not_1_out;

  not not_1 (not_1_out, in_2);
  and and_1 (and_1_out, in_1, not_1_out);
  and and_2 (and_2_out, in_1, in_2);
  // rs_latch rs_latch_1: pin names not known; wires that end beside it: and_1_out, and_2_out, out_3, out_4
endmodule

module d_flip_flop (
  input  D,
  input  C,
  output out_3,
  output out_4
);

  wire d_latch2_1_out_3, not_1_out;

  d_latch2 d_latch2_1 (.in_1(D), .in_2(C), .out_3(d_latch2_1_out_3));  // open: out_4
  not not_1 (not_1_out, C);
  d_latch2 d_latch2_2 (.in_1(d_latch2_1_out_3), .in_2(not_1_out), .out_3(out_3), .out_4(out_4));
endmodule

module d_flip_flop_we (
  input  D,
  input  C,
  input  WE,
  output out_4
);

  wire d_latch2_1_out_3, multiplexer_1_out, not_1_out;

  Multiplexer #(.enable("false")) multiplexer_1 (.in0(out_4), .in1(D), .out(multiplexer_1_out), .sel(WE));
  d_latch2 d_latch2_1 (.in_1(multiplexer_1_out), .in_2(C), .out_3(d_latch2_1_out_3));  // open: out_4
  not not_1 (not_1_out, C);
  d_latch2 d_latch2_2 (.in_1(d_latch2_1_out_3), .in_2(not_1_out), .out_3(out_4));  // open: out_4
endmodule

module eight_bit_register (
  input  [7:0] in_1,
  input  C,
  input  WE,
  output [7:0] out_4
);

  d_flip_flop_we d_flip_flop_we_1 (.D(in_1[0]), .C(C), .WE(WE), .out_4(out_4[0]));
  d_flip_flop_we d_flip_flop_we_2 (.D(in_1[1]), .C(C), .WE(WE), .out_4(out_4[1]));
  d_flip_flop_we d_flip_flop_we_3 (.D(in_1[2]), .C(C), .WE(WE), .out_4(out_4[2]));
  d_flip_flop_we d_flip_flop_we_4 (.D(in_1[2]), .C(C), .WE(WE), .out_4(out_4[2]));
  d_flip_flop_we d_flip_flop_we_5 (.D(in_1[3]), .C(C), .WE(WE), .out_4(out_4[3]));
  d_flip_flop_we d_flip_flop_we_6 (.D(in_1[4]), .C(C), .WE(WE), .out_4(out_4[4]));
  d_flip_flop_we d_flip_flop_we_7 (.D(in_1[5]), .C(C), .WE(WE), .out_4(out_4[5]));
  d_flip_flop_we d_flip_flop_we_8 (.D(in_1[6]), .C(C), .WE(WE), .out_4(out_4[6]));
  d_flip_flop_we d_flip_flop_we_9 (.D(in_1[7]), .C(C), .WE(WE), .out_4(out_4[7]));

  // Notes on the sheet:
  //   Data
endmodule

module register_file (
  input  [2:0] in_1,
  input  [2:0] in_2,
  input  [2:0] in_3,
  input  in_4,
  input  in_5,
  input  [7:0] in_6
);

  wire decoder_1_out0, decoder_1_out1, decoder_1_out2, decoder_1_out3, decoder_1_out4, decoder_1_out5,
       decoder_1_out6, decoder_1_out7;
  wire [7:0] eight_bit_register_1_out_4, eight_bit_register_2_out_4, eight_bit_register_3_out_4,
       eight_bit_register_4_out_4, eight_bit_register_5_out_4, eight_bit_register_6_out_4,
       eight_bit_register_7_out_4;

  eight_bit_register eight_bit_register_1 (.out_4(eight_bit_register_1_out_4));  // open: in_1, C, WE
  eight_bit_register eight_bit_register_2 (.out_4(eight_bit_register_2_out_4));  // open: in_1, C, WE
  eight_bit_register eight_bit_register_3 (.out_4(eight_bit_register_3_out_4));  // open: in_1, C, WE
  eight_bit_register eight_bit_register_4 (.out_4(eight_bit_register_4_out_4));  // open: in_1, C, WE
  eight_bit_register eight_bit_register_5 (.out_4(eight_bit_register_5_out_4));  // open: in_1, C, WE
  eight_bit_register eight_bit_register_6 (.out_4(eight_bit_register_6_out_4));  // open: in_1, C, WE
  eight_bit_register eight_bit_register_7 (.out_4(eight_bit_register_7_out_4));  // open: in_1, C, WE
  Decoder #(.select(3), .enable("false")) decoder_1 (
    .out0(decoder_1_out0), .out1(decoder_1_out1), .out2(decoder_1_out2), .out3(decoder_1_out3),
    .out4(decoder_1_out4), .out5(decoder_1_out5), .out6(decoder_1_out6), .out7(decoder_1_out7));  // open: sel
  Controlled_Buffer #(.width(8)) controlled_buffer_1 (.in({8{1'b0}}), .en(decoder_1_out0));  // open: out
  Controlled_Buffer #(.width(8)) controlled_buffer_2 (
    .in(eight_bit_register_1_out_4), .en(decoder_1_out1));  // open: out
  Controlled_Buffer #(.width(8)) controlled_buffer_3 (
    .in(eight_bit_register_2_out_4), .en(decoder_1_out2));  // open: out
  Controlled_Buffer #(.width(8)) controlled_buffer_4 (
    .in(eight_bit_register_4_out_4), .en(decoder_1_out4));  // open: out
  Controlled_Buffer #(.width(8)) controlled_buffer_5 (
    .in(eight_bit_register_3_out_4), .en(decoder_1_out3));  // open: out
  Controlled_Buffer #(.width(8)) controlled_buffer_6 (
    .in(eight_bit_register_5_out_4), .en(decoder_1_out5));  // open: out
  Controlled_Buffer #(.width(8)) controlled_buffer_7 (
    .in(eight_bit_register_6_out_4), .en(decoder_1_out6));  // open: out
  Controlled_Buffer #(.width(8)) controlled_buffer_8 (
    .in(eight_bit_register_7_out_4), .en(decoder_1_out7));  // open: out
endmodule
