// Logisim project lv2_alu.circ as structural Verilog
module add1b (
  input  A,
  input  B,
  input  Cin,
  output R,
  output Cout
);

  wire and_1_out, and_2_out, and_3_out, and_4_out, and_5_out, and_6_out, and_7_out, not_1_out, not_2_out,
       not_3_out, not_4_out, not_5_out, not_6_out;

  not not_1 (not_1_out, A);
  not not_2 (not_2_out, B);
  not not_3 (not_3_out, A);
  not not_4 (not_4_out, Cin);
  not not_5 (not_5_out, B);
  not not_6 (not_6_out, Cin);
  and and_1 (and_1_out, B, Cin);
  and and_2 (and_2_out, A, Cin);
  and and_3 (and_3_out, A, B);
  and and_4 (and_4_out, not_1_out, not_2_out, Cin);
  and and_5 (and_5_out, not_3_out, B, not_4_out);
  and and_6 (and_6_out, A, not_5_out, not_6_out);
  and and_7 (and_7_out, A, B, Cin);
  or or_1 (Cout, and_1_out, and_2_out, and_3_out);
  or or_2 (R, and_4_out, and_5_out, and_6_out, and_7_out);
endmodule

module add2b (
  input  [1:0] in_1,
  input  [1:0] in_2,
  output [1:0] out_3
);

  wire add1b_1_cout;

  add1b add1b_1 (.A(in_1[0]), .B(in_2[0]), .R(out_3[0]), .Cout(add1b_1_cout));  // open: Cin
  add1b add1b_2 (.A(in_1[1]), .B(in_2[1]), .Cin(add1b_1_cout), .R(out_3[1]));  // open: Cout
endmodule

module add4b (
  input  [3:0] in_1,
  input  in_2,
  input  [3:0] in_3,
  output [3:0] out_4,
  output out_5
);

  wire add1b_1_cout, add1b_2_cout, add1b_3_cout;

  add1b add1b_1 (.A(in_1[0]), .B(in_3[0]), .Cin(in_2), .R(out_4[0]), .Cout(add1b_1_cout));
  add1b add1b_2 (.A(in_1[1]), .B(in_3[1]), .Cin(add1b_1_cout), .R(out_4[1]), .Cout(add1b_2_cout));
  add1b add1b_3 (.A(in_1[2]), .B(in_3[2]), .Cin(add1b_2_cout), .R(out_4[2]), .Cout(add1b_3_cout));
  add1b add1b_4 (.A(in_1[3]), .B(in_3[3]), .Cin(add1b_3_cout), .R(out_4[3]), .Cout(out_5));

  // Notes on the sheet:
  //   A
  //   Cin
  //   B
endmodule

module alu (
  input  [3:0] A,
  input  [3:0] B,
  input  [3:0] Control,
  output [3:0] out_4
);

  wire [1:0] alu_ctrl_1_sl;
  wire [3:0] add4b_1_out_4, and_1_out, or_1_out, xor_1_out, xor_2_out;
  wire [3:3] alu_ctrl_1_as;

  alu_ctrl alu_ctrl_1 (.CTRL(Control), .AS(alu_ctrl_1_as[3]), .SL(alu_ctrl_1_sl));
  assign xor_1_out = B ^ {4{alu_ctrl_1_as[3]}};  // XOR_Gate xor_1, 4 bits wide
  add4b add4b_1 (.in_1(A), .in_2(alu_ctrl_1_as[3]), .in_3(xor_1_out), .out_4(add4b_1_out_4));  // open: out_5
  assign and_1_out = A & B;  // AND_Gate and_1, 4 bits wide
  assign or_1_out = A | B;  // OR_Gate or_1, 4 bits wide
  assign xor_2_out = A ^ B;  // XOR_Gate xor_2, 4 bits wide
  Multiplexer #(.select(2), .width(4), .enable("false")) multiplexer_1 (
    .in0(add4b_1_out_4), .in1(and_1_out), .in2(or_1_out), .in3(xor_2_out), .out(out_4), .sel(alu_ctrl_1_sl));
endmodule

module alu_ctrl (
  input  [3:0] CTRL,
  output AS,
  output [1:0] SL
);

  wire and_1_out, and_2_out, not_1_out;

  and and_1 (and_1_out, CTRL[2], not_1_out);
  not not_1 (not_1_out, CTRL[1]);
  and and_2 (and_2_out, CTRL[3], CTRL[1]);
  not not_2 (SL[0], CTRL[1]);
  or or_1 (SL[1], and_1_out, and_2_out);

  assign AS = CTRL[2];
endmodule
