// Logisim project lv2_cpu_finished.circ as structural Verilog: 4 circuits, main circuit main
module main (
  input  Reset,
  input  clk,
  input  in_3
);

  wire main_control_1_load, main_control_1_memtoreg, main_control_1_regwrite, main_control_1_store, or_1_out,
       registerfile_1_p6;
  wire [3:0] funt_to_alu_1_out_2, multiplexer_1_out, opcode_to_alu_1_out_2;
  wire [4:0] mipsprogramrom_1_p1_3, mipsprogramrom_1_p1_4, multiplexer_2_out;
  wire [5:0] mipsprogramrom_1_p1, mipsprogramrom_1_p1_6;
  wire [10:6] mipsprogramrom_1_p1_2;
  wire [23:0] mips_alu_1_p5;
  wire [25:21] mipsprogramrom_1_p1_5;
  wire [31:0] bit_extender_1_out, mips_alu_1_p2, mips_ram_1_p7, mipsprogramrom_1_p2, register_1_q,
       registerfile_1_p7;
  wire [31:2] incrementer_1_p4;
  wire [31:24] mips_alu_1_p5_2;

  Register #(.width(32), .trigger("falling")) register_1 (
    .D({incrementer_1_p4, 2'b00}), .en(1'b1), .clk(clk), .Q(register_1_q), .clr(Reset));
  funt_to_alu funt_to_alu_1 (.in_1(mipsprogramrom_1_p1), .out_2(funt_to_alu_1_out_2));
  opcode_to_alu opcode_to_alu_1 (.in_1(mipsprogramrom_1_p1_6), .out_2(opcode_to_alu_1_out_2));
  Multiplexer #(.width(4), .enable("false")) multiplexer_1 (
    .in0(funt_to_alu_1_out_2), .in1(opcode_to_alu_1_out_2), .out(multiplexer_1_out), .sel(or_1_out));
  // Incrementer #(.width(30)) incrementer_1: pin names not known; wires that end beside it: 1'b1, register_1_q, register_1_q[31:2], incrementer_1_p4
  main_control main_control_1 (
    .in_1(mipsprogramrom_1_p1_6), .RegWrite(main_control_1_regwrite), .Store(main_control_1_store),
    .Load(main_control_1_load), .MemToReg(main_control_1_memtoreg));
  // MIPSProgramROM mipsprogramrom_1: pin names not known; wires that end beside it: {mipsprogramrom_1_p1_6, mipsprogramrom_1_p1_5, mipsprogramrom_1_p1_4, mipsprogramrom_1_p1_3, mipsprogramrom_1_p1_2, mipsprogramrom_1_p1}, mipsprogramrom_1_p2
  or or_1 (or_1_out, mipsprogramrom_1_p1_6[0], mipsprogramrom_1_p1_6[1], mipsprogramrom_1_p1_6[2], mipsprogramrom_1_p1_6[3], mipsprogramrom_1_p1_6[4], mipsprogramrom_1_p1_6[5]);
  assign bit_extender_1_out = {{16{mipsprogramrom_1_p1_3[4]}}, {mipsprogramrom_1_p1_3, mipsprogramrom_1_p1_2, mipsprogramrom_1_p1}};  // Bit_Extender bit_extender_1
  Multiplexer #(.width(5), .enable("false")) multiplexer_2 (
    .in0(mipsprogramrom_1_p1_3), .in1(mipsprogramrom_1_p1_4), .out(multiplexer_2_out), .sel(or_1_out));
  // RegisterFile #(.trigger("falling")) registerfile_1: pin names not known; wires that end beside it: clk, main_control_1_regwrite, multiplexer_2_out, mipsprogramrom_1_p1_5, mipsprogramrom_1_p1_4, registerfile_1_p6, registerfile_1_p7
  Multiplexer #(.width(32), .enable("false")) multiplexer_3 (
    .in0({mips_alu_1_p5_2, mips_alu_1_p5}), .in1(mips_ram_1_p7), .out(mipsprogramrom_1_p2),
    .sel(main_control_1_memtoreg));
  // Mips_ALU mips_alu_1: pin names not known; wires that end beside it: registerfile_1_p6, mips_alu_1_p2, multiplexer_1_out, mipsprogramrom_1_p1_2, {mips_alu_1_p5_2, mips_alu_1_p5}
  Multiplexer #(.width(32), .enable("false")) multiplexer_4 (
    .in0(registerfile_1_p7), .in1(bit_extender_1_out), .out(mips_alu_1_p2), .sel(or_1_out));
  // MIPS_RAM #(.addrWidth(24)) mips_ram_1: pin names not known; wires that end beside it: mips_alu_1_p5, registerfile_1_p7, main_control_1_store, clk, main_control_1_load, in_3, mips_ram_1_p7

  // Notes on the sheet:
  //   opcode
  //   RS
  //   RT
  //   RD
  //   shamt
  //   funct
  //   imm
  //   contents of mipsprogramrom_1 (hex, n*v repeats v):
  //   addiu $t1, $0, 0xA or $t2, $t0, $t1 sll $t3, $t2, 3 sw $t3, 0($0) lw $t4, 0($0)
  //   RegWrite Signal
  //   AluOP
  //   Store
  //   Load
  //   Clear
  //   MemToReg
endmodule

module main_control (
  input  [5:0] in_1,
  output RegWrite,
  output Store,
  output Load,
  output MemToReg
);

  wire not_1_out, not_2_out, not_3_out;

  not not_1 (not_1_out, in_1[3]);
  not not_2 (not_2_out, in_1[1]);
  and and_1 (Store, in_1[5], in_1[3]);
  not not_3 (not_3_out, in_1[3]);
  or or_1 (RegWrite, not_1_out, not_2_out);
  and and_2 (Load, not_3_out, in_1[1]);

  assign MemToReg = in_1[1];
endmodule

module opcode_to_alu (
  input  [5:0] in_1,
  output [3:0] out_2
);

  wire not_1_out, not_2_out, not_3_out, not_4_out, not_5_out, not_6_out;

  not not_1 (not_1_out, in_1[3]);
  not not_2 (not_2_out, in_1[1]);
  not not_3 (not_3_out, in_1[3]);
  not not_4 (not_4_out, in_1[1]);
  not not_5 (not_5_out, in_1[3]);
  not not_6 (not_6_out, in_1[1]);
  and and_1 (out_2[3], not_1_out, not_2_out);
  and and_2 (out_2[2], not_3_out, not_4_out);
  and and_3 (out_2[0], not_5_out, not_6_out);

  assign out_2[1] = 1'b1;

  // Notes on the sheet:
  //   opcode
endmodule

module funt_to_alu (
  input  [5:0] in_1,
  output [3:0] out_2
);


  assign out_2 = {in_1[2], 1'b0, in_1[0], 1'b0};

  // Notes on the sheet:
  //   funct
  //   aluop
endmodule
