// Logisim project mips_cpu_freestyle.circ as structural Verilog: 9 circuits, main circuit main
module main (
  input  reset_PC,
  input  in_2,
  input  clk
);

  wire ins_to_alu_op_1_jr, main_ctrl_1_b_input, main_ctrl_1_beq, main_ctrl_1_bne, main_ctrl_1_ext_op,
       main_ctrl_1_j, main_ctrl_1_jal, main_ctrl_1_load, main_ctrl_1_mem_to_reg, main_ctrl_1_reg_dest,
       main_ctrl_1_reg_write, main_ctrl_1_store, next_pc_1_pc_src, zero_handler_1_zero;
  wire [3:0] ins_to_alu_op_1_aluop;
  wire [4:0] mipsprogramrom_1_p1_3, mipsprogramrom_1_p1_4, mipsprogramrom_1_p1_5, multiplexer_2_out,
       multiplexer_3_out;
  wire [5:0] mipsprogramrom_1_p1, mipsprogramrom_1_p1_6;
  wire [10:6] mipsprogramrom_1_p1_2;
  wire [23:0] mips_alu_1_p5;
  wire [29:0] next_pc_1_next_address;
  wire [31:0] extender_1_imm32, mips_ram_1_p7, multiplexer_1_out, multiplexer_4_out, multiplexer_5_out,
       next_address_1_pc, register_1_q, registerfile_1_p7, registerfile_1_p8;
  wire [31:2] incrementer_1_p3;
  wire [31:24] mips_alu_1_p5_2;

  Register #(.width(32), .trigger("falling")) register_1 (
    .D(next_address_1_pc), .en(1'b1), .clk(clk), .Q(register_1_q), .clr(reset_PC));
  next_address next_address_1 (
    .jr(ins_to_alu_op_1_jr), .pc_src(next_pc_1_pc_src), .jr_addr(registerfile_1_p7),
    .next_pc_addr(next_pc_1_next_address), .PC_plus_1(incrementer_1_p3), .pc(next_address_1_pc));
  // Incrementer #(.width(30)) incrementer_1: pin names not known; wires that end beside it: register_1_q, register_1_q[31:2], incrementer_1_p3
  // MIPSProgramROM mipsprogramrom_1: pin names not known; wires that end beside it: {mipsprogramrom_1_p1_6, mipsprogramrom_1_p1_5, mipsprogramrom_1_p1_4, mipsprogramrom_1_p1_3, mipsprogramrom_1_p1_2, mipsprogramrom_1_p1}
  // Probe on mipsprogramrom_1_p1_6
  main_ctrl main_ctrl_1 (
    .j(main_ctrl_1_j), .load(main_ctrl_1_load), .store(main_ctrl_1_store),
    .mem_to_reg(main_ctrl_1_mem_to_reg), .B_input(main_ctrl_1_b_input), .reg_write(main_ctrl_1_reg_write),
    .ext_op(main_ctrl_1_ext_op), .reg_dest(main_ctrl_1_reg_dest), .opcode(mipsprogramrom_1_p1_6),
    .jal(main_ctrl_1_jal), .beq(main_ctrl_1_beq), .bne(main_ctrl_1_bne));
  next_pc next_pc_1 (
    .next_address(next_pc_1_next_address), .zero(zero_handler_1_zero), .bne(main_ctrl_1_bne),
    .beq(main_ctrl_1_beq), .j(main_ctrl_1_j),
    .imm26({mipsprogramrom_1_p1_5, mipsprogramrom_1_p1_4, mipsprogramrom_1_p1_3, mipsprogramrom_1_p1_2, mipsprogramrom_1_p1}),
    .pc_plus_1(incrementer_1_p3), .pc_src(next_pc_1_pc_src));
  // Probe on mipsprogramrom_1_p1
  // Probe on mipsprogramrom_1_p1_5
  // Probe on mipsprogramrom_1_p1_4
  // Probe on mipsprogramrom_1_p1_3
  // Probe on mipsprogramrom_1_p1_2
  // Probe on {mipsprogramrom_1_p1_3, mipsprogramrom_1_p1_2, mipsprogramrom_1_p1}
  ins_to_alu_op ins_to_alu_op_1 (
    .jr(ins_to_alu_op_1_jr), .aluop(ins_to_alu_op_1_aluop), .funct(mipsprogramrom_1_p1),
    .opcode(mipsprogramrom_1_p1_6));
  Multiplexer #(.width(32), .enable("false")) multiplexer_1 (
    .in0(multiplexer_5_out), .in1({incrementer_1_p3, 2'b00}), .out(multiplexer_1_out), .sel(main_ctrl_1_jal));
  Multiplexer #(.width(5), .enable("false")) multiplexer_2 (
    .in0(mipsprogramrom_1_p1_4), .in1(mipsprogramrom_1_p1_3), .out(multiplexer_2_out),
    .sel(main_ctrl_1_reg_dest));
  Multiplexer #(.width(5), .enable("false")) multiplexer_3 (
    .in0(multiplexer_2_out), .in1({5{1'b1}}), .out(multiplexer_3_out), .sel(main_ctrl_1_jal));
  // RegisterFile #(.trigger("falling")) registerfile_1: pin names not known; wires that end beside it: multiplexer_1_out, clk, main_ctrl_1_reg_write, multiplexer_3_out, mipsprogramrom_1_p1_5, mipsprogramrom_1_p1_4, registerfile_1_p7, registerfile_1_p8
  extender extender_1 (
    .imm32(extender_1_imm32), .ext_op(main_ctrl_1_ext_op),
    .imm16({mipsprogramrom_1_p1_3, mipsprogramrom_1_p1_2, mipsprogramrom_1_p1}));
  Multiplexer #(.width(32), .enable("false")) multiplexer_4 (
    .in0(registerfile_1_p8), .in1(extender_1_imm32), .out(multiplexer_4_out), .sel(main_ctrl_1_b_input));
  // Mips_ALU mips_alu_1: pin names not known; wires that end beside it: registerfile_1_p7, multiplexer_4_out, ins_to_alu_op_1_aluop, mipsprogramrom_1_p1_2, {mips_alu_1_p5_2, mips_alu_1_p5}
  zero_handler zero_handler_1 (.zero(zero_handler_1_zero), .alu_result({mips_alu_1_p5_2, mips_alu_1_p5}));
  Multiplexer #(.width(32), .enable("false")) multiplexer_5 (
    .in0({mips_alu_1_p5_2, mips_alu_1_p5}), .in1(mips_ram_1_p7), .out(multiplexer_5_out),
    .sel(main_ctrl_1_mem_to_reg));
  // MIPS_RAM #(.addrWidth(24)) mips_ram_1: pin names not known; wires that end beside it: mips_alu_1_p5, registerfile_1_p8, main_ctrl_1_store, clk, main_ctrl_1_load, in_2, mips_ram_1_p7

  // Notes on the sheet:
  //   contents of mipsprogramrom_1 (hex, n*v repeats v):
  //   funkcija: subu $2, $4, $5 jr $31  main: addiu $8, $0, 4 ori $9, $0, 0xabcd sll $9, $9, 16 ori $9,
  //   $9, 0x1234 sw $9, 0($8) sw $9, 4($8) ori $10, $0, 4 addu $12, $8, $10 lw $13, 0($12) addu $5, $0,
  //   $13 bne   $5, $0, razlicito addiu $4, $5, -8 j     krajif razlicito: addiu $4, $5, 8 krajif:  jal
  //   funkcija sw $2, 8($8)  # Nakon izvrsenja programa u RAM memoriji bi trebalo da budu podaci: # adresa
  //   0: 0xabcd1234 # adresa 4: 0xabcd1234 # adresa 8: 0x00000008 # Ako je na adresi 8 vrijednost
  //   0xfffffff8 onda branch ne radi kako bi trebalo
  //   opcode
  //   RS
  //   RT
  //   RD
  //   shamt
  //   funct
  //   imm16
  //   imm26
  //   clear_RAM
endmodule

module extender (
  input  [15:0] imm16,
  input  ext_op,
  output [31:0] imm32
);

  wire [31:0] bit_extender_1_out, bit_extender_2_out;

  assign bit_extender_1_out = {{16{1'b0}}, imm16};  // Bit_Extender bit_extender_1
  assign bit_extender_2_out = {{16{imm16[15]}}, imm16};  // Bit_Extender bit_extender_2
  Multiplexer #(.width(32), .enable("false")) multiplexer_1 (
    .in0(bit_extender_1_out), .in1(bit_extender_2_out), .out(imm32), .sel(ext_op));
endmodule

module main_ctrl (
  input  [5:0] opcode,
  output reg_dest,
  output ext_op,
  output reg_write,
  output B_input,
  output mem_to_reg,
  output store,
  output load,
  output j,
  output jal,
  output beq,
  output bne
);

  wire and_3_out, and_4_out, and_5_out, and_6_out, not_1_out, not_2_out, not_3_out, not_4_out, not_5_out,
       not_6_out, not_7_out, not_8_out, not_9_out, not_10_out, not_11_out, not_12_out, not_13_out,
       not_14_out, not_15_out, not_16_out, not_17_out, not_18_out;

  not not_1 (not_1_out, opcode[2]);
  not not_2 (not_2_out, opcode[0]);
  not not_3 (not_3_out, opcode[2]);
  not not_4 (not_4_out, opcode[1]);
  not not_5 (not_5_out, opcode[2]);
  not not_6 (not_6_out, opcode[1]);
  not not_7 (not_7_out, opcode[3]);
  not not_8 (not_8_out, opcode[2]);
  not not_9 (not_9_out, opcode[5]);
  or or_1 (B_input, opcode[3], opcode[5]);
  not not_10 (not_10_out, opcode[3]);
  and and_1 (store, opcode[5], opcode[3]);
  not not_11 (not_11_out, opcode[3]);
  not not_12 (not_12_out, opcode[5]);
  not not_13 (not_13_out, opcode[3]);
  not not_14 (not_14_out, opcode[5]);
  not not_15 (not_15_out, opcode[3]);
  not not_16 (not_16_out, opcode[0]);
  not not_17 (not_17_out, opcode[3]);
  not not_18 (not_18_out, opcode[1]);
  and and_2 (reg_dest, not_1_out, not_2_out);
  and and_3 (and_3_out, not_3_out, not_4_out);
  and and_4 (and_4_out, not_5_out, not_6_out);
  and and_5 (and_5_out, not_7_out, not_8_out, opcode[0]);
  and and_6 (and_6_out, not_9_out, opcode[3]);
  and and_7 (mem_to_reg, opcode[5], not_10_out);
  and and_8 (load, opcode[5], not_11_out);
  and and_9 (j, not_12_out, not_13_out, opcode[1]);
  and and_10 (jal, not_14_out, opcode[1], opcode[0]);
  and and_11 (beq, not_15_out, opcode[2], not_16_out);
  and and_12 (bne, not_17_out, not_18_out, opcode[0]);
  or or_2 (ext_op, and_3_out, opcode[5]);
  or or_3 (reg_write, and_4_out, and_5_out, and_6_out);
endmodule

module ins_to_alu_op (
  input  [5:0] opcode,
  input  [5:0] funct,
  output [3:0] aluop,
  output jr
);

  wire funct_to_aluop_1_jr, nor_1_out;
  wire [3:0] funct_to_aluop_1_aluop, opcode_to_aluop_1_aluop;

  opcode_to_aluop opcode_to_aluop_1 (.opcode(opcode), .aluop(opcode_to_aluop_1_aluop));
  funct_to_aluop funct_to_aluop_1 (.funct(funct), .aluop(funct_to_aluop_1_aluop), .jr(funct_to_aluop_1_jr));
  nor nor_1 (nor_1_out, opcode[0], opcode[1], opcode[2], opcode[3], opcode[4], opcode[5]);
  Multiplexer #(.width(4), .enable("false")) multiplexer_1 (
    .in0(opcode_to_aluop_1_aluop), .in1(funct_to_aluop_1_aluop), .out(aluop), .sel(nor_1_out));
  and and_1 (jr, funct_to_aluop_1_jr, nor_1_out);
endmodule

module funct_to_aluop (
  input  [5:0] funct,
  output [3:0] aluop,
  output jr
);

  wire not_1_out;

  and and_1 (aluop[1], funct[5], funct[0]);
  not not_1 (not_1_out, funct[5]);
  and and_2 (aluop[0], not_1_out, funct[0]);

  assign aluop[3:2] = funct[2:1];
  assign jr = funct[3];
endmodule

module opcode_to_aluop (
  input  [5:0] opcode,
  output [3:0] aluop
);

  wire and_2_out, and_3_out, not_1_out, not_2_out, not_3_out, not_4_out;

  and and_1 (aluop[3], opcode[3], opcode[2]);
  not not_1 (not_1_out, opcode[3]);
  not not_2 (not_2_out, opcode[1]);
  not not_3 (not_3_out, opcode[0]);
  not not_4 (not_4_out, opcode[3]);
  and and_2 (and_2_out, not_1_out, not_2_out);
  and and_3 (and_3_out, opcode[1], not_3_out);
  or or_1 (aluop[1], not_4_out, opcode[0]);
  or or_2 (aluop[2], and_2_out, and_3_out);

  assign aluop[0] = 1'b0;
endmodule

module next_pc (
  input  [29:0] pc_plus_1,
  input  [25:0] imm26,
  input  j,
  input  beq,
  input  bne,
  input  zero,
  output [29:0] next_address,
  output pc_src
);

  wire and_1_out, and_2_out, and_3_out, not_1_out, not_2_out, not_3_out, not_4_out, not_5_out, not_6_out,
       not_7_out;
  wire [29:0] adder_1_out, bit_extender_1_out;

  not not_1 (not_1_out, j);
  not not_2 (not_2_out, beq);
  not not_3 (not_3_out, zero);
  not not_4 (not_4_out, j);
  not not_5 (not_5_out, bne);
  not not_6 (not_6_out, beq);
  not not_7 (not_7_out, bne);
  and and_1 (and_1_out, not_1_out, not_2_out, bne, not_3_out);
  and and_2 (and_2_out, not_4_out, beq, not_5_out, zero);
  or or_1 (pc_src, and_1_out, and_2_out, and_3_out);
  and and_3 (and_3_out, j, not_6_out, not_7_out);
  assign bit_extender_1_out = {{14{imm26[15]}}, imm26[15:0]};  // Bit_Extender bit_extender_1
  Adder #(.width(30)) adder_1 (.a(pc_plus_1), .b(bit_extender_1_out), .out(adder_1_out));  // open: cin, cout
  Multiplexer #(.width(30), .enable("false")) multiplexer_1 (
    .in0(adder_1_out), .in1({pc_plus_1[29:26], imm26}), .out(next_address), .sel(j));
endmodule

module zero_handler (
  input  [31:0] alu_result,
  output zero
);

  nor nor_1 (zero, alu_result[0], alu_result[1], alu_result[2], alu_result[3], alu_result[4], alu_result[5], alu_result[6], alu_result[7], alu_result[8], alu_result[9], alu_result[10], alu_result[11], alu_result[12], alu_result[13], alu_result[14], alu_result[15], alu_result[16], alu_result[17], alu_result[18], alu_result[19], alu_result[20], alu_result[21], alu_result[22], alu_result[23], alu_result[24], alu_result[25], alu_result[26], alu_result[27], alu_result[28], alu_result[29], alu_result[30], alu_result[31]);
endmodule

module next_address (
  input  [29:0] PC_plus_1,
  input  [29:0] next_pc_addr,
  input  [31:0] jr_addr,
  input  pc_src,
  input  jr,
  output [31:0] pc
);

  wire [29:0] multiplexer_1_out;

  Multiplexer #(.width(30), .enable("false")) multiplexer_1 (
    .in0(PC_plus_1), .in1(next_pc_addr), .out(multiplexer_1_out), .sel(pc_src));
  Multiplexer #(.width(32), .enable("false")) multiplexer_2 (
    .in0({multiplexer_1_out, 2'b00}), .in1(jr_addr), .out(pc), .sel(jr));
endmodule
