// Logisim project provjera.circ as structural Verilog: 6 circuits, main circuit main
module main (
  input  reset_pc,
  input  clk
);

  wire main_ctrl_1_j, main_ctrl_1_reg_write, r_i_handler_1_i_type, registerfile_1_p1, registerfile_1_p7;
  wire [3:0] funct_to_aluop_1_out_2, mips_alu_1_p3, opcode_to_aluop_1_alu_up;
  wire [4:0] mipsprogramrom_1_p1_2, multiplexer_1_out;
  wire [25:0] mipsprogramrom_1_p1;
  wire [29:0] incrementer_1_p3, next_pc_1_next_address;
  wire [31:0] bit_extender_1_out, mips_alu_1_p2, register_1_q, registerfile_1_p8;
  wire [31:26] mipsprogramrom_1_p1_3;

  Register #(.width(32), .trigger("falling")) register_1 (
    .D({next_pc_1_next_address, 2'b00}), .en(1'b1), .clk(clk), .Q(register_1_q), .clr(reset_pc));
  // Incrementer #(.width(30)) incrementer_1: pin names not known; wires that end beside it: register_1_q, register_1_q[31:2], incrementer_1_p3
  // MIPSProgramROM mipsprogramrom_1: pin names not known; wires that end beside it: {mipsprogramrom_1_p1_3, mipsprogramrom_1_p1[25:11], mipsprogramrom_1_p1_2, mipsprogramrom_1_p1[5:0]}
  next_pc next_pc_1 (
    .next_address(next_pc_1_next_address), .j(main_ctrl_1_j),
    .imm26({mipsprogramrom_1_p1[25:11], mipsprogramrom_1_p1_2, mipsprogramrom_1_p1[5:0]}),
    .pc_plus_1(incrementer_1_p3));
  assign bit_extender_1_out = {{16{mipsprogramrom_1_p1[15]}}, {mipsprogramrom_1_p1[15:11], mipsprogramrom_1_p1_2, mipsprogramrom_1_p1[5:0]}};  // Bit_Extender bit_extender_1
  main_ctrl main_ctrl_1 (.reg_write(main_ctrl_1_reg_write), .j(main_ctrl_1_j), .opcode(mipsprogramrom_1_p1_3));
  R_I_handler r_i_handler_1 (.i_type(r_i_handler_1_i_type), .opcode(mipsprogramrom_1_p1_3));
  Multiplexer #(.width(5), .enable("false")) multiplexer_1 (
    .in0(mipsprogramrom_1_p1[15:11]), .in1(mipsprogramrom_1_p1[20:16]), .out(multiplexer_1_out),
    .sel(r_i_handler_1_i_type));
  // RegisterFile #(.trigger("falling")) registerfile_1: pin names not known; wires that end beside it: registerfile_1_p1, clk, main_ctrl_1_reg_write, multiplexer_1_out, mipsprogramrom_1_p1[25:21], mipsprogramrom_1_p1[20:16], registerfile_1_p7, registerfile_1_p8
  funct_to_aluop funct_to_aluop_1 (.out_2(funct_to_aluop_1_out_2), .funct(mipsprogramrom_1_p1[5:0]));
  opcode_to_aluop opcode_to_aluop_1 (.opcode(mipsprogramrom_1_p1_3), .alu_up(opcode_to_aluop_1_alu_up));
  // Mips_ALU mips_alu_1: pin names not known; wires that end beside it: registerfile_1_p7, mips_alu_1_p2, mips_alu_1_p3, mipsprogramrom_1_p1_2, registerfile_1_p1
  Multiplexer #(.width(32), .enable("false")) multiplexer_2 (
    .in0(registerfile_1_p8), .in1(bit_extender_1_out), .out(mips_alu_1_p2), .sel(r_i_handler_1_i_type));
  Multiplexer #(.width(4), .enable("false")) multiplexer_3 (
    .in0(funct_to_aluop_1_out_2), .in1(opcode_to_aluop_1_alu_up), .out(mips_alu_1_p3),
    .sel(r_i_handler_1_i_type));

  // Notes on the sheet:
  //   contents of mipsprogramrom_1 (hex, n*v repeats v):
  //   addiu $4, $5, 4         sll $2, $4, 4   j foo
  //   opcode
  //   rs
  //   rt
  //   rd
  //   shamt
  //   imm16
  //   funct
endmodule

module opcode_to_aluop (
  input  [5:0] opcode,
  output [3:0] alu_up
);

  and and_1 (alu_up[1], opcode[0], opcode[3]);
  or or_1 (alu_up[3], opcode[1], opcode[2], opcode[4], opcode[5]);

  assign {alu_up[2], alu_up[0]} = {2{alu_up[3]}};
endmodule

module funct_to_aluop (
  input  [5:0] funct,
  output [3:0] out_2
);

  or or_1 (out_2[3], funct[0], funct[1], funct[2], funct[3], funct[4], funct[5]);

  assign out_2[2:0] = {3{out_2[3]}};
endmodule

module main_ctrl (
  input  [5:0] opcode,
  output j,
  output reg_write
);

  wire and_1_out, nor_1_out, nor_2_out;

  nor nor_1 (nor_1_out, opcode[0], opcode[1], opcode[2], opcode[3], opcode[4], opcode[5]);
  nor nor_2 (nor_2_out, opcode[2], opcode[0], opcode[3], opcode[4], opcode[5]);
  and and_1 (and_1_out, opcode[0], opcode[3]);
  and and_2 (j, nor_2_out, opcode[1]);
  or or_1 (reg_write, and_1_out, nor_1_out);
endmodule

module next_pc (
  input  [29:0] pc_plus_1,
  input  [25:0] imm26,
  input  j,
  output [29:0] next_address
);

  Multiplexer #(.width(30), .enable("false")) multiplexer_1 (
    .in0(pc_plus_1), .in1({pc_plus_1[29:26], imm26}), .out(next_address), .sel(j));
endmodule

module R_I_handler (
  input  [5:0] opcode,
  output i_type
);

  or or_1 (i_type, opcode[0], opcode[1], opcode[2], opcode[3], opcode[4], opcode[5]);
endmodule
