// Logisim project register_file.circ as structural Verilog: 5 circuits, main circuit rs_latch
module rs_latch (
  input  R,
  input  S,
  output Q,
  output Q_prime
);

  nor nor_1 (Q, R, Q_prime);
  nor nor_2 (Q_prime, Q, S);
endmodule

module d_latch (
  input  E,
  input  D,
  output out_3,
  output out_4
);

  wire and_1_out, and_2_out, not_1_out;

  not not_1 (not_1_out, D);
  and and_1 (and_1_out, not_1_out, E);
  and and_2 (and_2_out, E, D);
  rs_latch rs_latch_1 (.R(and_1_out), .S(and_2_out), .Q(out_3), .Q_prime(out_4));
endmodule

module d_flip_flop (
  input  WE,
  input  E,
  input  D,
  output Q_prime,
  output Q
);

  wire d_latch_1_out_4, multiplexer_1_out, not_1_out, not_2_out;

  not not_1 (not_1_out, WE);
  Multiplexer #(.enable("false")) multiplexer_1 (.in0(E), .in1(D), .out(multiplexer_1_out), .sel(not_1_out));
  d_latch d_latch_1 (.E(multiplexer_1_out), .D(D), .out_4(d_latch_1_out_4));  // open: out_3
  not not_2 (not_2_out, multiplexer_1_out);
  d_latch d_latch_2 (.E(not_2_out), .D(d_latch_1_out_4), .out_3(Q_prime), .out_4(Q));
endmodule

module eight_bit_register (
  input  [7:0] in_1,
  input  C,
  input  WE,
  output [7:0] out_4
);

  d_flip_flop d_flip_flop_1 (.WE(WE), .E(C), .D(in_1[0]), .Q(out_4[0]));  // open: Q_prime
  d_flip_flop d_flip_flop_2 (.WE(WE), .E(C), .D(in_1[1]), .Q(out_4[1]));  // open: Q_prime
  d_flip_flop d_flip_flop_3 (.WE(WE), .E(C), .D(in_1[2]), .Q(out_4[2]));  // open: Q_prime
  d_flip_flop d_flip_flop_4 (.WE(WE), .E(C), .D(in_1[3]), .Q(out_4[3]));  // open: Q_prime
  d_flip_flop d_flip_flop_5 (.WE(WE), .E(C), .D(in_1[4]), .Q(out_4[4]));  // open: Q_prime
  d_flip_flop d_flip_flop_6 (.WE(WE), .E(C), .D(in_1[5]), .Q(out_4[5]));  // open: Q_prime
  d_flip_flop d_flip_flop_7 (.WE(WE), .E(C), .D(in_1[6]), .Q(out_4[6]));  // open: Q_prime
  d_flip_flop d_flip_flop_8 (.WE(WE), .E(C), .D(in_1[7]), .Q(out_4[7]));  // open: Q_prime

  // Notes on the sheet:
  //   DataIn
  //   DataOut
endmodule

module register_file (
  input  [2:0] RA,
  input  [2:0] RB,
  input  [2:0] RW,
  input  RegWrite,
  input  Clk,
  input  [7:0] BusW,
  output [7:0] BusA,
  output [7:0] out_8
);

  wire and_1_out, and_2_out, and_3_out, and_4_out, and_5_out, and_6_out, and_7_out, decoder_1_out1,
       decoder_1_out2, decoder_1_out3, decoder_1_out4, decoder_1_out5, decoder_1_out6, decoder_1_out7,
       decoder_2_out0, decoder_2_out1, decoder_2_out2, decoder_2_out3, decoder_2_out4, decoder_2_out5,
       decoder_2_out6, decoder_2_out7, decoder_3_out0, decoder_3_out1, decoder_3_out2, decoder_3_out3,
       decoder_3_out4, decoder_3_out5, decoder_3_out6, decoder_3_out7;
  wire [7:0] eight_bit_register_1_out_4, eight_bit_register_2_out_4, eight_bit_register_3_out_4,
       eight_bit_register_4_out_4, eight_bit_register_5_out_4, eight_bit_register_6_out_4,
       eight_bit_register_7_out_4;

  Decoder #(.select(3)) decoder_1 (
    .out1(decoder_1_out1), .out2(decoder_1_out2), .out3(decoder_1_out3), .out4(decoder_1_out4),
    .out5(decoder_1_out5), .out6(decoder_1_out6), .out7(decoder_1_out7), .sel(RW));  // open: out0, en
  and and_1 (and_1_out, decoder_1_out1, RegWrite);
  and and_2 (and_2_out, decoder_1_out2, RegWrite);
  and and_3 (and_3_out, decoder_1_out3, RegWrite);
  and and_4 (and_4_out, decoder_1_out4, RegWrite);
  and and_5 (and_5_out, decoder_1_out5, RegWrite);
  and and_6 (and_6_out, decoder_1_out6, RegWrite);
  and and_7 (and_7_out, decoder_1_out7, RegWrite);
  eight_bit_register eight_bit_register_1 (.in_1(BusW), .C(Clk), .WE(and_1_out), .out_4(eight_bit_register_1_out_4));
  eight_bit_register eight_bit_register_2 (.in_1(BusW), .C(Clk), .WE(and_2_out), .out_4(eight_bit_register_2_out_4));
  eight_bit_register eight_bit_register_3 (.in_1(BusW), .C(Clk), .WE(and_3_out), .out_4(eight_bit_register_3_out_4));
  eight_bit_register eight_bit_register_4 (.in_1(BusW), .C(Clk), .WE(and_4_out), .out_4(eight_bit_register_4_out_4));
  eight_bit_register eight_bit_register_5 (.in_1(BusW), .C(Clk), .WE(and_5_out), .out_4(eight_bit_register_5_out_4));
  eight_bit_register eight_bit_register_6 (.in_1(BusW), .C(Clk), .WE(and_6_out), .out_4(eight_bit_register_6_out_4));
  eight_bit_register eight_bit_register_7 (.in_1(BusW), .C(Clk), .WE(and_7_out), .out_4(eight_bit_register_7_out_4));
  assign BusA = decoder_2_out1 ? eight_bit_register_1_out_4 : 8'bz;  // Controlled_Buffer controlled_buffer_1
  assign BusA = decoder_2_out2 ? eight_bit_register_2_out_4 : 8'bz;  // Controlled_Buffer controlled_buffer_2
  assign BusA = decoder_2_out3 ? eight_bit_register_3_out_4 : 8'bz;  // Controlled_Buffer controlled_buffer_3
  assign BusA = decoder_2_out4 ? eight_bit_register_4_out_4 : 8'bz;  // Controlled_Buffer controlled_buffer_4
  assign BusA = decoder_2_out5 ? eight_bit_register_5_out_4 : 8'bz;  // Controlled_Buffer controlled_buffer_5
  assign BusA = decoder_2_out6 ? eight_bit_register_6_out_4 : 8'bz;  // Controlled_Buffer controlled_buffer_6
  assign BusA = decoder_2_out7 ? eight_bit_register_7_out_4 : 8'bz;  // Controlled_Buffer controlled_buffer_7
  Decoder #(.select(3)) decoder_2 (
    .out0(decoder_2_out0), .out1(decoder_2_out1), .out2(decoder_2_out2), .out3(decoder_2_out3),
    .out4(decoder_2_out4), .out5(decoder_2_out5), .out6(decoder_2_out6), .out7(decoder_2_out7), .sel(RA));  // open: en
  assign BusA = decoder_2_out0 ? {8{1'b0}} : 8'bz;  // Controlled_Buffer controlled_buffer_8
  assign out_8 = decoder_3_out1 ? eight_bit_register_1_out_4 : 8'bz;  // Controlled_Buffer controlled_buffer_9
  assign out_8 = decoder_3_out2 ? eight_bit_register_2_out_4 : 8'bz;  // Controlled_Buffer controlled_buffer_10
  assign out_8 = decoder_3_out3 ? eight_bit_register_3_out_4 : 8'bz;  // Controlled_Buffer controlled_buffer_11
  assign out_8 = decoder_3_out4 ? eight_bit_register_4_out_4 : 8'bz;  // Controlled_Buffer controlled_buffer_12
  assign out_8 = decoder_3_out5 ? eight_bit_register_5_out_4 : 8'bz;  // Controlled_Buffer controlled_buffer_13
  assign out_8 = decoder_3_out6 ? eight_bit_register_6_out_4 : 8'bz;  // Controlled_Buffer controlled_buffer_14
  assign out_8 = decoder_3_out7 ? eight_bit_register_7_out_4 : 8'bz;  // Controlled_Buffer controlled_buffer_15
  Decoder #(.select(3)) decoder_3 (
    .out0(decoder_3_out0), .out1(decoder_3_out1), .out2(decoder_3_out2), .out3(decoder_3_out3),
    .out4(decoder_3_out4), .out5(decoder_3_out5), .out6(decoder_3_out6), .out7(decoder_3_out7), .sel(RB));  // open: en
  assign out_8 = decoder_3_out0 ? {8{1'b0}} : 8'bz;  // Controlled_Buffer controlled_buffer_16
endmodule
